// Logisim project decodificador_de_instrução.circ as structural Verilog: 2 circuits, main circuit decodificador_de_instrução
module \decodificador_de_instrução  (
  input  [31:0] \Instrução ,
  output [5:0] opcode,
  output [4:0] RS,
  output [4:0] RT,
  output [4:0] RD,
  output [4:0] shamt,
  output [5:0] funct,
  output [15:0] imm,
  output [25:0] addr
);

  wire decodificador_opcode_1_addi, decodificador_opcode_1_beq, decodificador_opcode_1_bne,
       decodificador_opcode_1_j, decodificador_opcode_1_jal, decodificador_opcode_1_lw,
       decodificador_opcode_1_mfc0, decodificador_opcode_1_mtc0, decodificador_opcode_1_r,
       decodificador_opcode_1_rfe, decodificador_opcode_1_sw, OP_I, OP_J, OP_R;
  wire [4:0] multiplexer_1_out, multiplexer_2_out;
  wire [25:0] demultiplexer_1_out0, demultiplexer_2_out0;
  wire [25:16] I_INTRUCAO_SEM_OP, R_INTRUCAO_SEM_OP;

  Demultiplexer #(.width(26)) demultiplexer_1 (
    .out0(demultiplexer_1_out0), .out1(addr), .in(demultiplexer_2_out0), .sel(OP_J));  // open: en
  Demultiplexer #(.width(26)) demultiplexer_2 (
    .out0(demultiplexer_2_out0), .out1({R_INTRUCAO_SEM_OP, RD, shamt, funct}), .in(\Instrução [25:0]),
    .sel(OP_R));  // open: en
  Demultiplexer #(.width(26)) demultiplexer_3 (
    .out1({I_INTRUCAO_SEM_OP, imm}), .in(demultiplexer_1_out0), .sel(OP_I));  // open: out0, en
  Decodificador_Opcode decodificador_opcode_1 (
    .R(decodificador_opcode_1_r), .J(decodificador_opcode_1_j), .RFE(decodificador_opcode_1_rfe),
    .MTC0(decodificador_opcode_1_mtc0), .MFC0(decodificador_opcode_1_mfc0), .Opcode(\Instrução [31:26]),
    .JAL(decodificador_opcode_1_jal), .ADDi(decodificador_opcode_1_addi), .LW(decodificador_opcode_1_lw),
    .SW(decodificador_opcode_1_sw), .BEQ(decodificador_opcode_1_beq), .BNE(decodificador_opcode_1_bne));
  or or_1 (OP_R, decodificador_opcode_1_r, decodificador_opcode_1_mtc0, decodificador_opcode_1_mfc0);
  or or_2 (OP_J, decodificador_opcode_1_j, decodificador_opcode_1_jal, decodificador_opcode_1_rfe);
  or or_3 (OP_I, decodificador_opcode_1_addi, decodificador_opcode_1_lw, decodificador_opcode_1_sw, decodificador_opcode_1_beq, decodificador_opcode_1_bne);
  Multiplexer #(.width(5)) multiplexer_1 (
    .in0({5{1'b0}}), .in1(R_INTRUCAO_SEM_OP[25:21]), .out(multiplexer_1_out), .sel(OP_R));  // open: en
  Multiplexer #(.width(5)) multiplexer_2 (
    .in0({5{1'b0}}), .in1(R_INTRUCAO_SEM_OP[20:16]), .out(multiplexer_2_out), .sel(OP_R));  // open: en
  Multiplexer #(.width(5)) multiplexer_3 (
    .in0(multiplexer_1_out), .in1(I_INTRUCAO_SEM_OP[25:21]), .out(RS), .sel(OP_I));  // open: en
  Multiplexer #(.width(5)) multiplexer_4 (
    .in0(multiplexer_2_out), .in1(I_INTRUCAO_SEM_OP[20:16]), .out(RT), .sel(OP_I));  // open: en

  assign opcode = \Instrução [31:26];

  // Other names for the same wires on the sheet: I_imm[15:0] = imm; I_INTRUCAO_SEM_OP[15:0] = imm;
  //   I_RS[4:0] = I_INTRUCAO_SEM_OP[25:21]; I_RT[4:0] = I_INTRUCAO_SEM_OP[20:16]; J_addr[25:0] = addr;
  //   J_INTRUCAO_SEM_OP[25:0] = addr; R_FUNC[5:0] = funct; R_INTRUCAO_SEM_OP[15:0] = {RD, shamt, funct};
  //   R_RD[4:0] = RD; R_RS[4:0] = R_INTRUCAO_SEM_OP[25:21]; R_RT[4:0] = R_INTRUCAO_SEM_OP[20:16]; R_SH[4:0] = shamt
endmodule

module main (
);

  \decodificador_de_instrução  \decodificador_de_instrução_1  ();  // open: Instrução, opcode, RS, RT, RD, shamt, funct, imm, addr
endmodule
