// Logisim project Decodificador_Opcode.circ as structural Verilog: 2 circuits, main circuit main
module main (
);

  Decodificador_Opcode decodificador_opcode_1 ();  // open: R, J, RFE, MTC0, MFC0, Opcode, JAL, ADDi, LW, SW, BEQ, BNE
endmodule

module Decodificador_Opcode (
  input  [5:0] Opcode,
  output R,
  output J,
  output JAL,
  output ADDi,
  output LW,
  output SW,
  output BEQ,
  output BNE,
  output RFE,
  output MTC0,
  output MFC0
);

  and u_R (R, ~Opcode[5], ~Opcode[4], ~Opcode[3], ~Opcode[2], ~Opcode[1], ~Opcode[0]);  // AND_Gate
  and u_J (J, ~Opcode[5], ~Opcode[4], ~Opcode[3], ~Opcode[2], Opcode[1], ~Opcode[0]);  // AND_Gate
  and u_JAL (JAL, ~Opcode[5], ~Opcode[4], ~Opcode[3], ~Opcode[2], Opcode[1], Opcode[0]);  // AND_Gate
  and u_ADDI (ADDi, ~Opcode[5], ~Opcode[4], Opcode[3], ~Opcode[2], ~Opcode[1], ~Opcode[0]);  // AND_Gate
  and u_LW (LW, Opcode[5], ~Opcode[4], ~Opcode[3], ~Opcode[2], Opcode[1], Opcode[0]);  // AND_Gate
  and u_SW (SW, Opcode[5], ~Opcode[4], Opcode[3], ~Opcode[2], Opcode[1], Opcode[0]);  // AND_Gate
  and u_BEQ (BEQ, ~Opcode[5], ~Opcode[4], ~Opcode[3], Opcode[2], ~Opcode[1], ~Opcode[0]);  // AND_Gate
  and u_BNE (BNE, ~Opcode[5], ~Opcode[4], ~Opcode[3], Opcode[2], ~Opcode[1], Opcode[0]);  // AND_Gate
  and u_RFE (RFE, ~Opcode[5], ~Opcode[4], ~Opcode[3], ~Opcode[2], ~Opcode[1], Opcode[0]);  // AND_Gate
  and u_MTC0 (MTC0, ~Opcode[5], ~Opcode[4], ~Opcode[3], ~Opcode[2], Opcode[1], ~Opcode[0]);  // AND_Gate
  and u_MFC0 (MFC0, ~Opcode[5], ~Opcode[4], ~Opcode[3], ~Opcode[2], Opcode[1], Opcode[0]);  // AND_Gate
endmodule
