// Logisim project MIPS.circ as structural Verilog: 1 circuit, main circuit main
module main (
);

  wire and_1_out, Clock, exception_t, multiplexer_4_out, not_1_out, Zero;
  wire [4:0] multiplexer_8_out, multiplexer_9_out, rd, rs, rt, shamt, WR, WR_expect;
  wire [5:0] funct, opcode;
  wire [15:0] imm16;
  wire [25:0] addr;
  wire [31:0] adder_1_out, EPC, imm32, LD, LD1, LD2, mem_instr_1_output, mfc0R, multiplexer_1_out,
       multiplexer_2_out, multiplexer_3_out, multiplexer_5_out, multiplexer_6_out, multiplexer_7_out,
       multiplexer_10_out, multiplexer_13_out, multiplexer_14_out, PC_4, PC_q, result, WD;

  Multiplexer #(.width(32), .enable("false")) multiplexer_1 (
    .in0(multiplexer_2_out), .out(multiplexer_1_out), .sel(1'b0));  // open: in1
  Multiplexer #(.width(32), .enable("false")) multiplexer_2 (
    .in0(multiplexer_6_out), .in1(LD1), .out(multiplexer_2_out), .sel(1'b0));
  not not_1 (not_1_out, Zero);
  Multiplexer #(.width(32), .enable("false")) multiplexer_3 (
    .in0(multiplexer_1_out), .in1(32'h80000180), .out(multiplexer_3_out), .sel(1'b0));
  Multiplexer #(.enable("false")) multiplexer_4 (.in0(Zero), .in1(not_1_out), .out(multiplexer_4_out), .sel(1'b0));
  Multiplexer #(.width(32), .enable("false")) multiplexer_5 (
    .in0(multiplexer_3_out), .in1(EPC), .out(multiplexer_5_out), .sel(1'b0));
  Multiplexer #(.width(32), .enable("false")) multiplexer_6 (
    .in0(PC_4), .in1(adder_1_out), .out(multiplexer_6_out), .sel(and_1_out));
  and and_1 (and_1_out, multiplexer_4_out, 1'b0);
  Register #(.width(32)) PC (.D(multiplexer_5_out), .en(1'b1), .Q(PC_q), .clk(Clock), .clr(1'b0));
  Adder #(.width(32)) adder_1 (.a({imm32[29:0], 2'b00}), .b(PC_4), .out(adder_1_out));  // open: cin, cout
  Adder #(.width(32)) adder_2 (.a(32'h4), .b(PC_q), .out(PC_4));  // open: cin, cout
  mem_instr mem_instr_1 (.INPUT(PC_q), .OUTPUT(mem_instr_1_output));
  Multiplexer #(.width(32), .enable("false")) multiplexer_7 (
    .in0(result), .in1(LD1), .out(multiplexer_7_out), .sel(1'b0));
  Clock clock_1 (.out(Clock));
  \decodificador_de_instrução  \decodificador_de_instrução_1  (
    .\Instrução (mem_instr_1_output), .opcode(opcode), .RS(rs), .RT(rt), .RD(rd), .shamt(shamt),
    .funct(funct), .imm(imm16), .addr(addr));
  contole_excecao_main main_1 (
    .CLK(Clock), .WriteRes(1'b0), .except(exception_t), .EPC_in(PC_4), .WR_in(WR),
    .res_data(multiplexer_7_out), .EPC(EPC), .WR_out(WR_expect), .MFC0_out(mfc0R));
  Multiplexer #(.width(5), .enable("false")) multiplexer_8 (.in0(rt), .in1(rd), .out(multiplexer_8_out), .sel(1'b0));
  Multiplexer #(.width(5), .enable("false")) multiplexer_9 (
    .in0(multiplexer_8_out), .in1(WR_expect), .out(multiplexer_9_out), .sel(1'b0));
  Multiplexer #(.width(32), .enable("false")) multiplexer_10 (
    .in0(multiplexer_13_out), .in1(mfc0R), .out(multiplexer_10_out), .sel(1'b0));
  extensor extensor_1 (.INPUT(imm16), .OUTPUT(imm32));
  Multiplexer #(.width(5), .enable("false")) multiplexer_11 (
    .in0(multiplexer_9_out), .in1({5{1'b1}}), .out(WR), .sel(1'b0));
  Multiplexer #(.width(32), .enable("false")) multiplexer_12 (
    .in0(multiplexer_10_out), .in1(PC_4), .out(WD), .sel(1'b0));
  banco_de_registradores banco_de_registradores_1 (
    .CLK(Clock), .EW(1'b0), .WD(WD), .LR1(rs), .LR2(rt), .WR(WR), .LD1(LD1), .LD2(LD2));
  Multiplexer #(.width(32), .enable("false")) multiplexer_13 (
    .in0(result), .in1(LD), .out(multiplexer_13_out), .sel(1'b0));
  ULA ula_1 (
    .Result(result), .Overflow(exception_t), .Zero(Zero), .A(LD1), .B(multiplexer_14_out), .Shamt(shamt),
    .\Operação (4'b0000));
  Multiplexer #(.width(32), .enable("false")) multiplexer_14 (
    .in0(LD2), .in1(imm32), .out(multiplexer_14_out), .sel(1'b0));
  mem_data mem_data_1 (.address(result), .\input (LD2), .str(1'b0), .ld(1'b0), .clk(Clock), .\output (LD));
endmodule
