// Logisim project Unidade_de_Controle_Principal.circ as structural Verilog: 2 circuits, main circuit main
module main (
);

  unidade_de_controle_principal unidade_de_controle_principal_1 ();  // open: RegDst, WriteReg, ExcOut, WriteRegEx, ALUOp, Opcode
  unidade_de_controle_principal unidade_de_controle_principal_2 ();  // open: RegDst, WriteReg, ExcOut, WriteRegEx, ALUOp, Opcode
  // Decodificador_Opcode decodificador_opcode_1: pin names not known
endmodule

module unidade_de_controle_principal (
  input  [5:0] Opcode,
  output RegDst,
  output WriteReg,
  output ExcOut,
  output WriteRegEx,
  output [1:0] ALUOp
);

  wire decodificador_opcode_1_i, decodificador_opcode_1_j, decodificador_opcode_1_mfc0,
       decodificador_opcode_1_mtc0, decodificador_opcode_1_r, decodificador_opcode_1_rfe;
  wire [5:0] multiplexer_1_out, multiplexer_2_out, multiplexer_3_out, multiplexer_4_out, multiplexer_5_out;

  Decodificador_Opcode decodificador_opcode_1 (
    .R(decodificador_opcode_1_r), .J(decodificador_opcode_1_j), .I(decodificador_opcode_1_i),
    .RFE(decodificador_opcode_1_rfe), .MTC0(decodificador_opcode_1_mtc0), .MFC0(decodificador_opcode_1_mfc0),
    .Opcode(Opcode));
  Multiplexer #(.width(6)) multiplexer_1 (
    .in0({6{1'b0}}), .in1(6'b110000), .out(multiplexer_1_out), .sel(decodificador_opcode_1_r));  // open: en
  Multiplexer #(.width(6)) multiplexer_2 (
    .in0(multiplexer_1_out), .in1({6{1'b0}}), .out(multiplexer_2_out), .sel(decodificador_opcode_1_j));  // open: en
  Multiplexer #(.width(6)) multiplexer_3 (
    .in0(multiplexer_2_out), .in1({6{1'b0}}), .out(multiplexer_3_out), .sel(decodificador_opcode_1_i));  // open: en
  Multiplexer #(.width(6)) multiplexer_4 (
    .in0(multiplexer_3_out), .in1(6'b001000), .out(multiplexer_4_out), .sel(decodificador_opcode_1_rfe));  // open: en
  Multiplexer #(.width(6)) multiplexer_5 (
    .in0(multiplexer_4_out), .in1(6'b000100), .out(multiplexer_5_out), .sel(decodificador_opcode_1_mtc0));  // open: en
  Multiplexer #(.width(6)) multiplexer_6 (
    .in0(multiplexer_5_out), .in1(6'b010000), .out({RegDst, WriteReg, ExcOut, WriteRegEx, ALUOp}),
    .sel(decodificador_opcode_1_mfc0));  // open: en
endmodule
